// Digital circuit pong.dig as structural Verilog
module pong (
  input  Physics
);

  wire _7408_1_pin3, _7408_1_pin6, _7408_1_pin8, _7408_1_pin11, _7408_2_pin3, _7408_2_pin4, _7408_2_pin6,
       _7408_2_pin8, _7408_2_pin9, _7408_2_pin10, _7408_2_pin12, _7408_3_pin3, _7408_3_pin6, _7408_3_pin8,
       _7408_3_pin9, _7408_3_pin11, _7408_3_pin12, _7408_4_pin3, _7408_4_pin4, _7408_4_pin6, _7408_4_pin8,
       _7408_4_pin9, _7408_4_pin10, _7408_4_pin12, _7408_5_pin2, _7408_5_pin3, _7408_5_pin6, _7408_5_pin9,
       _7408_6_pin3, _7408_6_pin8, _7430_1_pin6, _7430_1_pin8, _7430_1_pin11, _7430_1_pin12, _7430_2_pin1,
       _7430_2_pin2, _7430_2_pin3, _7430_2_pin4, _7430_2_pin6, _7430_2_pin8, _7430_2_pin12, _7430_3_pin1,
       _7430_3_pin2, _7430_3_pin3, _7430_3_pin4, _7430_3_pin8, _7430_4_pin1, _7430_4_pin2, _7430_4_pin5,
       _7430_4_pin6, _7430_4_pin8, _7430_4_pin11, _7430_4_pin12, _7430_5_pin8, _7430_6_pin8, _7430_7_pin8,
       _7430_7_pin12, _7430_8_pin8, _7430_9_pin8, _7430_10_pin1, _7430_10_pin2, _7430_10_pin3, _7430_10_pin4,
       _7430_10_pin5, _7430_10_pin6, _7430_10_pin8, _7430_10_pin11, _7430_11_pin1, _7430_11_pin2,
       _7430_11_pin3, _7430_11_pin4, _7430_11_pin5, _7432_1_pin13, _7432_2_pin6, _7474_1_pin10,
       _7474_1_pin13, _7474_2_pin10, _7474_2_pin13, _74163_1_pin15, _74163_2_pin15, _74163_4_pin15,
       _74163_5_pin15, _74163_7_pin1, _74163_7_pin15, _74163_8_pin12, _74163_9_pin15, _74163_10_pin12,
       _74191_1_pin11, _74191_1_pin13, _74191_1_pin14, _74191_2_pin13, _74191_4_pin13, _74191_5_pin13,
       _747266_1_pin3, _747266_1_pin4, _747266_1_pin10, _747266_1_pin11, _747266_2_pin3, _747266_2_pin4,
       _747266_2_pin10, _747266_2_pin11, _747266_3_pin3, _747266_3_pin4, _747266_3_pin10, _747266_3_pin11, B,
       CLK, H0, H1, H2, H3, H4, H5, H6, H7, H8, H9, H10, H11, HCLR, HSYNC, LDOW, LUP, MO, not_1_out,
       not_2_out, not_3_out, not_11_out, not_12_out, not_17_out, not_19_out, not_21_out, not_34_out,
       not_35_out, not_36_out, not_37_out, not_38_out, not_39_out, not_40_out, not_49_out, not_50_out,
       not_51_out, not_52_out, not_53_out, not_54_out, not_56_out, p1R, p1rx, p1ry, p2R, p2rx, p2ry, RDOW,
       RENDER, RESET, RUP, START, V0, V1, V2, V3, V4, V5, V6, V7, V8, V9, V10, V11, VCLR, VSYNC, Y1CLK,
       Y1DIR, Y2CLK, Y2DIR;
  wire [9:0] Y1, Y2, YSTART;

  Button W (.out(LUP));
  Button S (.out(LDOW));
  or or_1 (B, MO, p1R, p2R);
  Button I (.out(RUP));
  Button K (.out(RDOW));
  Button T (.out(START));
  Button Y (.out(RESET));
  not not_1 (not_1_out, START);
  not not_2 (not_2_out, RESET);
  D_FF_AS d_ff_as_1 (.Set(~not_1_out), .D(1'b0), .C(1'b0), .Clr(~not_2_out), .Q(RENDER));  // open: nQ
  VGA vga_1 (.R(B), .G(B), .B(B), .H(HSYNC), .V(VSYNC), .C(CLK));
  not not_3 (not_3_out, LDOW);
  _7408 _7408_1 (
    .pin1(LUP), .pin2(Physics), .pin3(_7408_1_pin3), .pin4(Physics), .pin5(LDOW), .pin6(_7408_1_pin6),
    .pin7(1'b0), .pin8(_7408_1_pin8), .pin9(RUP), .pin10(Physics), .pin11(_7408_1_pin11), .pin12(Physics),
    .pin13(RDOW), .pin14(1'b1));
  _7432 _7432_1 (
    .pin1(LUP), .pin2(not_3_out), .pin3(Y1DIR), .pin4(_7408_1_pin3), .pin5(_7408_1_pin6), .pin6(Y1CLK),
    .pin7(1'b0), .pin8(Y2CLK), .pin9(_7408_1_pin8), .pin10(_7408_1_pin11), .pin11(Y2DIR), .pin12(RUP),
    .pin13(_7432_1_pin13), .pin14(1'b1));
  not not_4 (_7432_1_pin13, RDOW);
  _74163 _74163_1 (
    .pin1(HCLR), .pin2(CLK), .pin3(1'b0), .pin4(1'b0), .pin5(1'b0), .pin6(1'b0), .pin7(1'b1), .pin8(1'b0),
    .pin9(1'b1), .pin10(1'b1), .pin11(H3), .pin12(H2), .pin13(H1), .pin14(H0), .pin15(_74163_1_pin15),
    .pin16(1'b1));
  _74163 _74163_2 (
    .pin1(HCLR), .pin2(CLK), .pin3(1'b0), .pin4(1'b0), .pin5(1'b0), .pin6(1'b0), .pin7(1'b1), .pin8(1'b0),
    .pin9(1'b1), .pin10(_74163_1_pin15), .pin11(H7), .pin12(H6), .pin13(H5), .pin14(H4),
    .pin15(_74163_2_pin15), .pin16(1'b1));
  _74163 _74163_3 (
    .pin1(HCLR), .pin2(CLK), .pin3(1'b0), .pin4(1'b0), .pin5(1'b0), .pin6(1'b0), .pin7(1'b1), .pin8(1'b0),
    .pin9(1'b1), .pin10(_74163_2_pin15), .pin11(H11), .pin12(H10), .pin13(H9), .pin14(H8), .pin16(1'b1));  // open: pin15
  _74163 _74163_4 (
    .pin1(VCLR), .pin2(HCLR), .pin3(1'b0), .pin4(1'b0), .pin5(1'b0), .pin6(1'b0), .pin7(1'b1), .pin8(1'b0),
    .pin9(1'b1), .pin10(1'b1), .pin11(V3), .pin12(V2), .pin13(V1), .pin14(V0), .pin15(_74163_4_pin15),
    .pin16(1'b1));
  _74163 _74163_5 (
    .pin1(VCLR), .pin2(HCLR), .pin3(1'b0), .pin4(1'b0), .pin5(1'b0), .pin6(1'b0), .pin7(1'b1), .pin8(1'b0),
    .pin9(1'b1), .pin10(_74163_4_pin15), .pin11(V7), .pin12(V6), .pin13(V5), .pin14(V4),
    .pin15(_74163_5_pin15), .pin16(1'b1));
  _74163 _74163_6 (
    .pin1(VCLR), .pin2(HCLR), .pin3(1'b0), .pin4(1'b0), .pin5(1'b0), .pin6(1'b0), .pin7(1'b1), .pin8(1'b0),
    .pin9(1'b1), .pin10(_74163_5_pin15), .pin11(V11), .pin12(V10), .pin13(V9), .pin14(V8), .pin16(1'b1));  // open: pin15
  _74191 _74191_1 (
    .pin1(YSTART[1]), .pin2(Y2[1]), .pin3(Y2[0]), .pin4(1'b0), .pin5(Y2DIR), .pin6(Y2[2]), .pin7(Y2[3]),
    .pin8(1'b0), .pin9(YSTART[3]), .pin10(YSTART[2]), .pin11(_74191_1_pin11), .pin13(_74191_1_pin13),
    .pin14(_74191_1_pin14), .pin15(YSTART[0]), .pin16(1'b1));  // open: pin12
  _74191 _74191_2 (
    .pin1(YSTART[5]), .pin2(Y2[5]), .pin3(Y2[4]), .pin4(_74191_1_pin13), .pin5(Y2DIR), .pin6(Y2[6]),
    .pin7(Y2[7]), .pin8(1'b0), .pin9(YSTART[7]), .pin10(YSTART[6]), .pin11(_74191_1_pin11),
    .pin13(_74191_2_pin13), .pin14(_74191_1_pin14), .pin15(YSTART[4]), .pin16(1'b1));  // open: pin12
  _74191 _74191_3 (
    .pin1(YSTART[9]), .pin2(Y2[9]), .pin3(Y2[8]), .pin4(_74191_2_pin13), .pin5(Y2DIR), .pin8(1'b0),
    .pin9(1'b0), .pin10(1'b0), .pin11(_74191_1_pin11), .pin14(_74191_1_pin14), .pin15(YSTART[8]), .pin16(1'b1));  // open: pin6, pin7, pin12, pin13
  _7430 _7430_1 (
    .pin1(H0), .pin2(H1), .pin3(H2), .pin4(H3), .pin5(H4), .pin6(_7430_1_pin6), .pin7(1'b0),
    .pin8(_7430_1_pin8), .pin11(_7430_1_pin11), .pin12(_7430_1_pin12), .pin14(1'b1));  // open: pin9, pin10, pin13
  not not_5 (_7430_1_pin6, H5);
  _7430 _7430_2 (
    .pin1(_7430_2_pin1), .pin2(_7430_2_pin2), .pin3(_7430_2_pin3), .pin4(_7430_2_pin4), .pin5(H4),
    .pin6(_7430_2_pin6), .pin7(1'b0), .pin8(_7430_2_pin8), .pin11(H7), .pin12(_7430_2_pin12), .pin14(1'b1));  // open: pin9, pin10, pin13
  not not_6 (_7430_2_pin1, H0);
  not not_7 (_7430_2_pin2, H1);
  not not_8 (_7430_2_pin3, H2);
  not not_9 (_7430_2_pin4, H3);
  not not_10 (_7430_2_pin6, H5);
  not not_11 (not_11_out, H8);
  _7408 _7408_2 (
    .pin1(not_11_out), .pin2(H9), .pin3(_7408_2_pin3), .pin4(_7408_2_pin4), .pin5(_7408_2_pin3),
    .pin6(_7408_2_pin6), .pin7(1'b0), .pin8(_7408_2_pin8), .pin9(_7408_2_pin9), .pin10(_7408_2_pin10),
    .pin11(_7408_2_pin9), .pin12(_7408_2_pin12), .pin13(H9), .pin14(1'b1));
  not not_12 (not_12_out, _7408_2_pin6);
  _7430 _7430_3 (
    .pin1(_7430_3_pin1), .pin2(_7430_3_pin2), .pin3(_7430_3_pin3), .pin4(_7430_3_pin4), .pin5(H4), .pin6(H5),
    .pin7(1'b0), .pin8(_7430_3_pin8), .pin11(H7), .pin12(H6), .pin14(1'b1));  // open: pin9, pin10, pin13
  not not_13 (_7430_3_pin1, H0);
  not not_14 (_7430_3_pin2, H1);
  not not_15 (_7430_3_pin3, H2);
  not not_16 (_7430_3_pin4, H3);
  not not_17 (not_17_out, _7430_1_pin8);
  not not_18 (_7408_2_pin4, _7430_2_pin8);
  not not_19 (not_19_out, _7408_2_pin8);
  not not_20 (_7408_2_pin10, _7430_3_pin8);
  not not_21 (not_21_out, START);
  not not_22 (_7430_1_pin12, H7);
  not not_23 (_7430_1_pin11, H6);
  not not_24 (_7430_2_pin12, H6);
  not not_25 (_7408_2_pin12, H8);
  not not_26 (_74191_1_pin11, START);
  _7432 _7432_2 (
    .pin1(START), .pin2(Y2CLK), .pin3(_74191_1_pin14), .pin4(START), .pin5(Y1CLK), .pin6(_7432_2_pin6),
    .pin7(1'b0), .pin9(1'b1), .pin10(1'b1), .pin12(1'b1), .pin13(1'b1), .pin14(1'b1));  // open: pin8, pin11
  _7408 _7408_3 (
    .pin1(H8), .pin2(H9), .pin3(_7408_3_pin3), .pin4(not_17_out), .pin5(_7408_3_pin3), .pin6(_7408_3_pin6),
    .pin7(1'b0), .pin8(_7408_3_pin8), .pin9(_7408_3_pin9), .pin10(V9), .pin11(_7408_3_pin11),
    .pin12(_7408_3_pin12), .pin13(_7408_3_pin8), .pin14(1'b1));
  not not_27 (HCLR, _7408_3_pin6);
  _7474 _7474_1 (
    .pin1(not_12_out), .pin2(1'b0), .pin3(1'b0), .pin4(not_19_out), .pin5(HSYNC), .pin7(1'b0), .pin9(VSYNC),
    .pin10(_7474_1_pin10), .pin11(1'b0), .pin12(1'b0), .pin13(_7474_1_pin13), .pin14(1'b1));  // open: pin6, pin8
  not not_28 (VCLR, _7408_3_pin11);
  not not_29 (_7408_3_pin9, V8);
  _7430 _7430_4 (
    .pin1(_7430_4_pin1), .pin2(_7430_4_pin2), .pin3(V2), .pin4(V3), .pin5(_7430_4_pin5), .pin6(_7430_4_pin6),
    .pin7(1'b0), .pin8(_7430_4_pin8), .pin11(_7430_4_pin11), .pin12(_7430_4_pin12), .pin14(1'b1));  // open: pin9, pin10, pin13
  not not_30 (_7430_4_pin1, V0);
  not not_31 (_7430_4_pin2, V1);
  not not_32 (_7430_4_pin5, V4);
  not not_33 (_7430_4_pin6, V5);
  not not_34 (not_34_out, V0);
  not not_35 (not_35_out, V2);
  not not_36 (not_36_out, V4);
  not not_37 (not_37_out, V9);
  not not_38 (not_38_out, V0);
  not not_39 (not_39_out, V1);
  not not_40 (not_40_out, V4);
  _7430 _7430_5 (
    .pin1(not_34_out), .pin2(V1), .pin3(not_35_out), .pin4(V3), .pin5(not_36_out), .pin6(V5), .pin7(1'b0),
    .pin8(_7430_5_pin8), .pin11(V7), .pin12(V6), .pin14(1'b1));  // open: pin9, pin10, pin13
  _7408 _7408_4 (
    .pin1(V8), .pin2(not_37_out), .pin3(_7408_4_pin3), .pin4(_7408_4_pin4), .pin5(_7408_4_pin3),
    .pin6(_7408_4_pin6), .pin7(1'b0), .pin8(_7408_4_pin8), .pin9(_7408_4_pin9), .pin10(_7408_4_pin10),
    .pin11(_7408_4_pin10), .pin12(_7408_4_pin12), .pin13(V8), .pin14(1'b1));
  not not_41 (_7474_1_pin13, _7408_4_pin6);
  _7430 _7430_6 (
    .pin1(not_38_out), .pin2(not_39_out), .pin3(V2), .pin4(V3), .pin5(not_40_out), .pin6(V5), .pin7(1'b0),
    .pin8(_7430_6_pin8), .pin11(V7), .pin12(V6), .pin14(1'b1));  // open: pin9, pin10, pin13
  _74191 _74191_4 (
    .pin1(YSTART[1]), .pin2(Y1[1]), .pin3(Y1[0]), .pin4(1'b0), .pin5(Y1DIR), .pin6(Y1[2]), .pin7(Y1[3]),
    .pin8(1'b0), .pin9(YSTART[3]), .pin10(YSTART[2]), .pin11(not_21_out), .pin13(_74191_4_pin13),
    .pin14(_7432_2_pin6), .pin15(YSTART[0]), .pin16(1'b1));  // open: pin12
  _74191 _74191_5 (
    .pin1(YSTART[5]), .pin2(Y1[5]), .pin3(Y1[4]), .pin4(_74191_4_pin13), .pin5(Y1DIR), .pin6(Y1[6]),
    .pin7(Y1[7]), .pin8(1'b0), .pin9(YSTART[7]), .pin10(YSTART[6]), .pin11(not_21_out),
    .pin13(_74191_5_pin13), .pin14(_7432_2_pin6), .pin15(YSTART[4]), .pin16(1'b1));  // open: pin12
  _74191 _74191_6 (
    .pin1(YSTART[9]), .pin2(Y1[9]), .pin3(Y1[8]), .pin4(_74191_5_pin13), .pin5(Y1DIR), .pin8(1'b0),
    .pin9(1'b0), .pin10(1'b0), .pin11(not_21_out), .pin14(_7432_2_pin6), .pin15(YSTART[8]), .pin16(1'b1));  // open: pin6, pin7, pin12, pin13
  not not_42 (_7408_3_pin12, _7430_4_pin8);
  not not_43 (_7430_4_pin12, V7);
  not not_44 (_7430_4_pin11, V6);
  not not_45 (_7408_4_pin4, _7430_5_pin8);
  not not_46 (_7408_4_pin12, V9);
  not not_47 (_7474_1_pin10, _7408_4_pin8);
  not not_48 (_7408_4_pin9, _7430_6_pin8);
  not not_49 (not_49_out, H0);
  not not_50 (not_50_out, H1);
  not not_51 (not_51_out, H2);
  not not_52 (not_52_out, H3);
  not not_53 (not_53_out, H4);
  not not_54 (not_54_out, H5);
  _7430 _7430_7 (
    .pin1(not_49_out), .pin2(not_50_out), .pin3(not_51_out), .pin4(not_52_out), .pin5(not_53_out),
    .pin6(not_54_out), .pin7(1'b0), .pin8(_7430_7_pin8), .pin11(H6), .pin12(_7430_7_pin12), .pin14(1'b1));  // open: pin9, pin10, pin13
  not not_55 (_7430_7_pin12, H7);
  not not_56 (not_56_out, _7430_7_pin8);
  _747266 _747266_1 (
    .pin1(H3), .pin2(1'b0), .pin3(_747266_1_pin3), .pin4(_747266_1_pin4), .pin5(H4), .pin6(1'b1),
    .pin7(1'b0), .pin8(H5), .pin9(1'b0), .pin10(_747266_1_pin10), .pin11(_747266_1_pin11), .pin12(H6),
    .pin13(1'b0), .pin14(1'b1));
  _747266 _747266_2 (
    .pin1(H7), .pin2(1'b0), .pin3(_747266_2_pin3), .pin4(_747266_2_pin4), .pin5(H8), .pin6(1'b0),
    .pin7(1'b0), .pin8(H9), .pin9(1'b0), .pin10(_747266_2_pin10), .pin11(_747266_2_pin11), .pin12(V5),
    .pin13(Y1[5]), .pin14(1'b1));
  _747266 _747266_3 (
    .pin1(V6), .pin2(Y1[6]), .pin3(_747266_3_pin3), .pin4(_747266_3_pin4), .pin5(V7), .pin6(Y1[7]),
    .pin7(1'b0), .pin8(V9), .pin9(Y1[9]), .pin10(_747266_3_pin10), .pin11(_747266_3_pin11), .pin12(V8),
    .pin13(Y1[8]), .pin14(1'b1));
  _7408 _7408_5 (
    .pin1(H8), .pin2(_7408_5_pin2), .pin3(_7408_5_pin3), .pin4(not_56_out), .pin5(_7408_5_pin3),
    .pin6(_7408_5_pin6), .pin7(1'b0), .pin8(MO), .pin9(_7408_5_pin9), .pin10(_7408_5_pin6),
    .pin11(_7408_5_pin9), .pin12(V3), .pin13(1'b1), .pin14(1'b1));
  not not_57 (_7408_5_pin2, H9);
  _7430 _7430_8 (
    .pin1(_747266_1_pin3), .pin2(_747266_1_pin4), .pin3(_747266_1_pin11), .pin4(_747266_1_pin10),
    .pin5(_747266_2_pin3), .pin6(_747266_2_pin4), .pin7(1'b0), .pin8(_7430_8_pin8), .pin11(1'b1),
    .pin12(_747266_2_pin10), .pin14(1'b1));  // open: pin9, pin10, pin13
  _7430 _7430_9 (
    .pin1(_747266_2_pin11), .pin2(_747266_3_pin3), .pin3(_747266_3_pin4), .pin4(_747266_3_pin11),
    .pin5(_747266_3_pin10), .pin6(_747266_3_pin10), .pin7(1'b0), .pin8(_7430_9_pin8), .pin11(1'b1),
    .pin12(1'b1), .pin14(1'b1));  // open: pin9, pin10, pin13
  not not_58 (p1rx, _7430_8_pin8);
  _74163 _74163_7 (
    .pin1(_74163_7_pin1), .pin2(HCLR), .pin3(1'b0), .pin4(1'b0), .pin5(1'b0), .pin6(1'b0), .pin7(p1ry),
    .pin8(1'b0), .pin9(p1ry), .pin10(p1ry), .pin15(_74163_7_pin15), .pin16(1'b1));  // open: pin11, pin12, pin13, pin14
  _74163 _74163_8 (
    .pin1(_74163_7_pin1), .pin2(HCLR), .pin3(1'b0), .pin4(1'b0), .pin5(1'b0), .pin6(1'b0), .pin7(p1ry),
    .pin8(1'b0), .pin9(p1ry), .pin10(_74163_7_pin15), .pin12(_74163_8_pin12), .pin16(1'b1));  // open: pin11, pin13, pin14, pin15
  not not_59 (_74163_7_pin1, _74163_8_pin12);
  _7474 _7474_2 (
    .pin1(_74163_7_pin1), .pin2(1'b0), .pin3(1'b0), .pin4(_7430_9_pin8), .pin5(p1ry), .pin7(1'b0),
    .pin9(p2ry), .pin10(_7474_2_pin10), .pin11(1'b0), .pin12(1'b0), .pin13(_7474_2_pin13), .pin14(1'b1));  // open: pin6, pin8
  _7408 _7408_6 (
    .pin1(p1ry), .pin2(p1rx), .pin3(_7408_6_pin3), .pin4(_7408_6_pin3), .pin5(RENDER), .pin6(p1R),
    .pin7(1'b0), .pin8(_7408_6_pin8), .pin9(p2rx), .pin10(p2ry), .pin11(p2R), .pin12(_7408_6_pin8),
    .pin13(RENDER), .pin14(1'b1));
  _74163 _74163_9 (
    .pin1(_7474_2_pin13), .pin2(HCLR), .pin3(1'b0), .pin4(1'b0), .pin5(1'b0), .pin6(1'b0), .pin7(p2ry),
    .pin8(1'b0), .pin9(p2ry), .pin10(p2ry), .pin15(_74163_9_pin15), .pin16(1'b1));  // open: pin11, pin12, pin13, pin14
  _74163 _74163_10 (
    .pin1(_7474_2_pin13), .pin2(HCLR), .pin3(1'b0), .pin4(1'b0), .pin5(1'b0), .pin6(1'b0), .pin7(p2ry),
    .pin8(1'b0), .pin9(p2ry), .pin10(_74163_9_pin15), .pin12(_74163_10_pin12), .pin16(1'b1));  // open: pin11, pin13, pin14, pin15
  not not_60 (_7474_2_pin13, _74163_10_pin12);
  _7430 _7430_10 (
    .pin1(_7430_10_pin1), .pin2(_7430_10_pin2), .pin3(_7430_10_pin3), .pin4(_7430_10_pin4),
    .pin5(_7430_10_pin5), .pin6(_7430_10_pin6), .pin7(1'b0), .pin8(_7430_10_pin8), .pin11(_7430_10_pin11),
    .pin12(1'b1), .pin14(1'b1));  // open: pin9, pin10, pin13
  _7430 _7430_11 (
    .pin1(_7430_11_pin1), .pin2(_7430_11_pin2), .pin3(_7430_11_pin3), .pin4(_7430_11_pin4),
    .pin5(_7430_11_pin5), .pin6(_7430_11_pin5), .pin7(1'b0), .pin8(_7474_2_pin10), .pin11(1'b1),
    .pin12(1'b1), .pin14(1'b1));  // open: pin9, pin10, pin13
  not not_61 (p2rx, _7430_10_pin8);
  _747266 _747266_4 (
    .pin1(H3), .pin2(1'b0), .pin3(_7430_10_pin1), .pin4(_7430_10_pin2), .pin5(H4), .pin6(1'b0), .pin7(1'b0),
    .pin8(H5), .pin9(1'b1), .pin10(_7430_10_pin4), .pin11(_7430_10_pin3), .pin12(H6), .pin13(1'b1),
    .pin14(1'b1));
  _747266 _747266_5 (
    .pin1(H7), .pin2(1'b0), .pin3(_7430_10_pin5), .pin4(_7430_10_pin6), .pin5(H8), .pin6(1'b0), .pin7(1'b0),
    .pin8(H9), .pin9(1'b1), .pin10(_7430_10_pin11), .pin11(_7430_11_pin1), .pin12(V5), .pin13(Y2[5]),
    .pin14(1'b1));
  _747266 _747266_6 (
    .pin1(V6), .pin2(Y2[6]), .pin3(_7430_11_pin2), .pin4(_7430_11_pin3), .pin5(V7), .pin6(Y2[7]),
    .pin7(1'b0), .pin8(V9), .pin9(Y2[9]), .pin10(_7430_11_pin5), .pin11(_7430_11_pin4), .pin12(V8),
    .pin13(Y2[8]), .pin14(1'b1));
  // also tied to GND on the sheet: {YSTART[0], YSTART[1], YSTART[3], YSTART[6], YSTART[8], YSTART[9]}
  // also tied to VCC on the sheet: {YSTART[2], YSTART[4], YSTART[5], YSTART[7]}

  // Other names for the same wires on the sheet: HCOUNT[9:0] = {H9, H8, H7, H6, H5, H4, H3, H2, H1, H0};
  //   PCLK = Physics; G = B; R = B; VCOUNT[9:0] = {V9, V8, V7, V6, V5, V4, V3, V2, V1, V0}

  // Notes on the sheet:
  //   Physics: Hz: 120
  //   I/O SUITE
  //   PADDLE CTRL
  //   COUNTERS
  //   VGA DRIVER
  //   CLR
  //   SYNC GEN
  //   PARTING (STATIC)
endmodule
